// Logisim project Unicycle.circ as structural Verilog: 14 circuits, main circuit main
module main (
);

  wire ALUSrc, Branch, button_1_out, clock0, clock_1_out, comparator_1_eq, Jump, MemtoReg, MemWrite, RegDst,
       RegWrite, uc_1_branch, ula_1_equal;
  wire [2:0] uc_ula_1_ulacode;
  wire [4:0] multiplexer_3_out;
  wire [9:0] adder_1_out, adder_2_out, multiplexer_1_out, multiplexer_2_out, register_1_q, rom_1_data;
  wire [19:0] ula_1_ula_out_2;
  wire [31:0] bit_extender_1_out, multiplexer_4_out, multiplexer_5_out, ram_1_dout,
       registerfile_1_read_data_1, registerfile_1_read_data_2, ula_1_ula_out;
  wire [31:10] rom_1_data_2;

  Register #(.width(10)) register_1 (
    .D(multiplexer_1_out), .en(1'b1), .clk(clock0), .Q(register_1_q), .clr(button_1_out));
  Button button_1 (.out(button_1_out));
  Multiplexer #(.width(10)) multiplexer_1 (
    .in0(multiplexer_2_out), .in1(rom_1_data), .out(multiplexer_1_out), .sel(Jump));
  Adder #(.width(10)) adder_1 (.a(10'h1), .b(register_1_q), .out(adder_1_out));  // open: cin, cout
  ROM #(.addrWidth(10), .dataWidth(32)) rom_1 (.addr(register_1_q), .data({rom_1_data_2, rom_1_data}));
  Adder #(.width(10)) adder_2 (.a(adder_1_out), .b(rom_1_data), .out(adder_2_out));  // open: cin, cout
  Multiplexer #(.width(10)) multiplexer_2 (.in0(adder_1_out), .in1(adder_2_out), .out(multiplexer_2_out), .sel(Branch));
  Comparator #(.width(32)) comparator_1 (
    .a({rom_1_data_2, rom_1_data}), .b({32{1'b0}}), .eq(comparator_1_eq));  // open: gt, lt
  Clock clock_1 (.out(clock_1_out));
  and NOP (clock0, ~comparator_1_eq, clock_1_out);  // AND_Gate
  Multiplexer #(.width(5)) multiplexer_3 (
    .in0(rom_1_data_2[15:11]), .in1(rom_1_data_2[20:16]), .out(multiplexer_3_out), .sel(RegDst));
  Multiplexer #(.width(32)) multiplexer_4 (
    .in0({ula_1_ula_out[31:22], ula_1_ula_out_2, ula_1_ula_out[1:0]}), .in1(ram_1_dout),
    .out(multiplexer_4_out), .sel(MemtoReg));
  UC uc_1 (
    .OpCode(rom_1_data_2[31:26]), .RegDst(RegDst), .Branch(uc_1_branch), .MemtoReg(MemtoReg),
    .MemWrite(MemWrite), .ALUSrc(ALUSrc), .RegWrite(RegWrite), .Jump(Jump));
  UC_ula uc_ula_1 (.funct(rom_1_data[5:0]), .OpCode(rom_1_data_2[31:26]), .ULAcode(uc_ula_1_ulacode));
  assign bit_extender_1_out = {{16{rom_1_data_2[15]}}, {rom_1_data_2[15:10], rom_1_data}};  // Bit_Extender bit_extender_1
  RegisterFile registerfile_1 (
    .Read_Register_1(rom_1_data_2[25:21]), .Read_Register_2(rom_1_data_2[20:16]),
    .Write_Data(multiplexer_4_out), .RegWrite(RegWrite), .Write_Register(multiplexer_3_out), .Clock(clock0),
    .Read_Data_1(registerfile_1_read_data_1), .Read_Data_2(registerfile_1_read_data_2));
  Multiplexer #(.width(32)) multiplexer_5 (
    .in0(registerfile_1_read_data_2), .in1(bit_extender_1_out), .out(multiplexer_5_out), .sel(ALUSrc));
  CacheMemory cachememory_1 ();  // open: cpu_address, cpu_mem_read, cpu_mem_write, mem_ready, clock, reset, mem_read_data, state_debug, cpu_ready, mem_address, mem_write_data, mem_read, mem_write, cpu_read_data
  RAM #(.addrWidth(20), .dataWidth(32), .enables("line"), .\type ("nonvolatile")) ram_1 (
    .addr(ula_1_ula_out_2), .we(MemWrite), .clk(clock0), .din(registerfile_1_read_data_2), .dout(ram_1_dout));
  RAM #(.addrWidth(20), .dataWidth(32)) ram_2 ();  // open: addr, we, oe, clk, din, dout
  and and_1 (Branch, uc_1_branch, ula_1_equal);
  ULA ula_1 (
    .A(registerfile_1_read_data_1), .B(multiplexer_5_out), .Op(uc_ula_1_ulacode),
    .shamt({rom_1_data_2[10], rom_1_data[9:6]}),
    .ULA_out({ula_1_ula_out[31:22], ula_1_ula_out_2, ula_1_ula_out[1:0]}), .Equal(ula_1_equal));

  // Notes on the sheet:
  //   contents of rom_1 (hex, n*v repeats v):
  //   24110000 24120028 2409820 8e290000 8e4a0000 ae490000 ae2a0000 26520004 26310004 12330001 8000c03
endmodule

module RegisterFile (
  input  [4:0] Read_Register_1,
  input  [4:0] Read_Register_2,
  input  [31:0] Write_Data,
  input  RegWrite,
  input  [4:0] Write_Register,
  input  Clock,
  output [31:0] Read_Data_1,
  output [31:0] Read_Data_2
);

  wire demultiplexer_1_out0, demultiplexer_1_out1, demultiplexer_1_out2, demultiplexer_1_out3,
       demultiplexer_1_out4, demultiplexer_1_out5, demultiplexer_1_out6, demultiplexer_1_out7,
       demultiplexer_1_out8, demultiplexer_1_out9, demultiplexer_1_out10, demultiplexer_1_out11,
       demultiplexer_1_out12, demultiplexer_1_out13, demultiplexer_1_out14, demultiplexer_1_out15,
       demultiplexer_1_out16, demultiplexer_1_out17, demultiplexer_1_out18, demultiplexer_1_out19,
       demultiplexer_1_out20, demultiplexer_1_out21, demultiplexer_1_out22, demultiplexer_1_out23,
       demultiplexer_1_out24, demultiplexer_1_out25, demultiplexer_1_out26, demultiplexer_1_out27,
       demultiplexer_1_out28, demultiplexer_1_out29, demultiplexer_1_out30, demultiplexer_1_out31;
  wire [31:0] register_1_q, register_2_q, register_3_q, register_4_q, register_5_q, register_6_q,
       register_7_q, register_8_q, register_9_q, register_10_q, register_11_q, register_12_q, register_13_q,
       register_14_q, register_15_q, register_16_q, register_17_q, register_18_q, register_19_q,
       register_20_q, register_21_q, register_22_q, register_23_q, register_24_q, register_25_q,
       register_26_q, register_27_q, register_28_q, register_29_q, register_30_q, register_31_q,
       register_32_q;

  Demultiplexer #(.enable("true"), .select(5)) demultiplexer_1 (
    .out0(demultiplexer_1_out0), .out1(demultiplexer_1_out1), .out2(demultiplexer_1_out2),
    .out3(demultiplexer_1_out3), .out4(demultiplexer_1_out4), .out5(demultiplexer_1_out5),
    .out6(demultiplexer_1_out6), .out7(demultiplexer_1_out7), .out8(demultiplexer_1_out8),
    .out9(demultiplexer_1_out9), .out10(demultiplexer_1_out10), .out11(demultiplexer_1_out11),
    .out12(demultiplexer_1_out12), .out13(demultiplexer_1_out13), .out14(demultiplexer_1_out14),
    .out15(demultiplexer_1_out15), .out16(demultiplexer_1_out16), .out17(demultiplexer_1_out17),
    .out18(demultiplexer_1_out18), .out19(demultiplexer_1_out19), .out20(demultiplexer_1_out20),
    .out21(demultiplexer_1_out21), .out22(demultiplexer_1_out22), .out23(demultiplexer_1_out23),
    .out24(demultiplexer_1_out24), .out25(demultiplexer_1_out25), .out26(demultiplexer_1_out26),
    .out27(demultiplexer_1_out27), .out28(demultiplexer_1_out28), .out29(demultiplexer_1_out29),
    .out30(demultiplexer_1_out30), .out31(demultiplexer_1_out31), .in(RegWrite), .sel(Write_Register));  // open: en
  Register #(.width(32)) register_1 (
    .D(Write_Data), .en(demultiplexer_1_out1), .Q(register_1_q), .clk(Clock));  // open: clr
  Register #(.width(32)) register_2 (
    .D(Write_Data), .en(demultiplexer_1_out0), .Q(register_2_q), .clk(Clock));  // open: clr
  Register #(.width(32)) register_3 (
    .D(Write_Data), .en(demultiplexer_1_out9), .Q(register_3_q), .clk(Clock));  // open: clr
  Register #(.width(32)) register_4 (
    .D(Write_Data), .en(demultiplexer_1_out8), .Q(register_4_q), .clk(Clock));  // open: clr
  Register #(.width(32)) register_5 (
    .D(Write_Data), .en(demultiplexer_1_out17), .Q(register_5_q), .clk(Clock));  // open: clr
  Register #(.width(32)) register_6 (
    .D(Write_Data), .en(demultiplexer_1_out16), .Q(register_6_q), .clk(Clock));  // open: clr
  Register #(.width(32)) register_7 (
    .D(Write_Data), .en(demultiplexer_1_out25), .Q(register_7_q), .clk(Clock));  // open: clr
  Register #(.width(32)) register_8 (
    .D(Write_Data), .en(demultiplexer_1_out24), .Q(register_8_q), .clk(Clock));  // open: clr
  Register #(.width(32)) register_9 (
    .D(Write_Data), .en(demultiplexer_1_out2), .Q(register_9_q), .clk(Clock));  // open: clr
  Register #(.width(32)) register_10 (
    .D(Write_Data), .en(demultiplexer_1_out10), .Q(register_10_q), .clk(Clock));  // open: clr
  Register #(.width(32)) register_11 (
    .D(Write_Data), .en(demultiplexer_1_out18), .Q(register_11_q), .clk(Clock));  // open: clr
  Register #(.width(32)) register_12 (
    .D(Write_Data), .en(demultiplexer_1_out26), .Q(register_12_q), .clk(Clock));  // open: clr
  Register #(.width(32)) register_13 (
    .D(Write_Data), .en(demultiplexer_1_out3), .Q(register_13_q), .clk(Clock));  // open: clr
  Register #(.width(32)) register_14 (
    .D(Write_Data), .en(demultiplexer_1_out11), .Q(register_14_q), .clk(Clock));  // open: clr
  Register #(.width(32)) register_15 (
    .D(Write_Data), .en(demultiplexer_1_out19), .Q(register_15_q), .clk(Clock));  // open: clr
  Register #(.width(32)) register_16 (
    .D(Write_Data), .en(demultiplexer_1_out27), .Q(register_16_q), .clk(Clock));  // open: clr
  Register #(.width(32)) register_17 (
    .D(Write_Data), .en(demultiplexer_1_out4), .Q(register_17_q), .clk(Clock));  // open: clr
  Register #(.width(32)) register_18 (
    .D(Write_Data), .en(demultiplexer_1_out12), .Q(register_18_q), .clk(Clock));  // open: clr
  Register #(.width(32)) register_19 (
    .D(Write_Data), .en(demultiplexer_1_out20), .Q(register_19_q), .clk(Clock));  // open: clr
  Register #(.width(32)) register_20 (
    .D(Write_Data), .en(demultiplexer_1_out28), .Q(register_20_q), .clk(Clock));  // open: clr
  Register #(.width(32)) register_21 (
    .D(Write_Data), .en(demultiplexer_1_out5), .Q(register_21_q), .clk(Clock));  // open: clr
  Register #(.width(32)) register_22 (
    .D(Write_Data), .en(demultiplexer_1_out13), .Q(register_22_q), .clk(Clock));  // open: clr
  Register #(.width(32)) register_23 (
    .D(Write_Data), .en(demultiplexer_1_out21), .Q(register_23_q), .clk(Clock));  // open: clr
  Register #(.width(32)) register_24 (
    .D(Write_Data), .en(demultiplexer_1_out29), .Q(register_24_q), .clk(Clock));  // open: clr
  Register #(.width(32)) register_25 (
    .D(Write_Data), .en(demultiplexer_1_out6), .Q(register_25_q), .clk(Clock));  // open: clr
  Register #(.width(32)) register_26 (
    .D(Write_Data), .en(demultiplexer_1_out14), .Q(register_26_q), .clk(Clock));  // open: clr
  Register #(.width(32)) register_27 (
    .D(Write_Data), .en(demultiplexer_1_out22), .Q(register_27_q), .clk(Clock));  // open: clr
  Register #(.width(32)) register_28 (
    .D(Write_Data), .en(demultiplexer_1_out30), .Q(register_28_q), .clk(Clock));  // open: clr
  Register #(.width(32)) register_29 (
    .D(Write_Data), .en(demultiplexer_1_out7), .Q(register_29_q), .clk(Clock));  // open: clr
  Register #(.width(32)) register_30 (
    .D(Write_Data), .en(demultiplexer_1_out15), .Q(register_30_q), .clk(Clock));  // open: clr
  Register #(.width(32)) register_31 (
    .D(Write_Data), .en(demultiplexer_1_out23), .Q(register_31_q), .clk(Clock));  // open: clr
  Register #(.width(32)) register_32 (
    .D(Write_Data), .en(demultiplexer_1_out31), .Q(register_32_q), .clk(Clock));  // open: clr
  Multiplexer #(.enable("true"), .select(5), .width(32)) multiplexer_1 (
    .in0({32{1'b0}}), .in1(register_1_q), .in2(register_9_q), .in3(register_13_q), .in4(register_17_q),
    .in5(register_21_q), .in6(register_25_q), .in7(register_29_q), .in8(register_4_q), .in9(register_3_q),
    .in10(register_10_q), .in11(register_14_q), .in12(register_18_q), .in13(register_22_q),
    .in14(register_26_q), .in15(register_30_q), .in16(register_6_q), .in17(register_5_q),
    .in18(register_11_q), .in19(register_15_q), .in20(register_19_q), .in21(register_23_q),
    .in22(register_27_q), .in23(register_31_q), .in24(register_8_q), .in25(register_7_q),
    .in26(register_12_q), .in27(register_16_q), .in28(register_20_q), .in29(register_24_q),
    .in30(register_28_q), .in31(register_32_q), .out(Read_Data_1), .sel(Read_Register_1));  // open: en
  Multiplexer #(.enable("true"), .select(5), .width(32)) multiplexer_2 (
    .in0({32{1'b0}}), .in1(register_1_q), .in2(register_9_q), .in3(register_13_q), .in4(register_17_q),
    .in5(register_21_q), .in6(register_25_q), .in7(register_29_q), .in8(register_4_q), .in9(register_3_q),
    .in10(register_10_q), .in11(register_14_q), .in12(register_18_q), .in13(register_22_q),
    .in14(register_26_q), .in15(register_30_q), .in16(register_6_q), .in17(register_5_q),
    .in18(register_11_q), .in19(register_15_q), .in20(register_19_q), .in21(register_23_q),
    .in22(register_27_q), .in23(register_31_q), .in24(register_8_q), .in25(register_7_q),
    .in26(register_12_q), .in27(register_16_q), .in28(register_20_q), .in29(register_24_q),
    .in30(register_28_q), .in31(register_32_q), .out(Read_Data_2), .sel(Read_Register_2));  // open: en
endmodule

module ULA (
  input  [31:0] A,
  input  [31:0] B,
  input  [2:0] Op,
  input  [4:0] shamt,
  output [31:0] ULA_out,
  output Equal
);

  wire comparator_1_lt;
  wire [31:0] adder_1_out, multiplexer_1_out, nor_1_out, shifter_1_out, subtractor_1_out;

  Adder #(.width(32)) adder_1 (.a(A), .b(B), .out(adder_1_out));  // open: cin, cout
  Subtractor #(.width(32)) subtractor_1 (.a(A), .b(B), .out(subtractor_1_out));  // open: bin, bout
  assign nor_1_out = ~(A | B);  // NOR_Gate nor_1, 32 bits wide
  Comparator #(.width(32)) comparator_1 (.a(A), .b(B), .eq(Equal), .lt(comparator_1_lt));  // open: gt
  Multiplexer #(.width(32)) multiplexer_1 (
    .in0({32{1'b0}}), .in1(32'h1), .out(multiplexer_1_out), .sel(comparator_1_lt));
  Shifter #(.width(32)) shifter_1 (.in(B), .\dist (shamt), .out(shifter_1_out));
  Multiplexer #(.select(3), .width(32)) multiplexer_2 (
    .in0(subtractor_1_out), .in1(nor_1_out), .in2(multiplexer_1_out), .in3(shifter_1_out), .in4(adder_1_out),
    .in5(adder_1_out), .in6(adder_1_out), .in7(adder_1_out), .out(ULA_out), .sel(Op));
endmodule

module UC (
  input  [5:0] OpCode,
  output RegDst,
  output Branch,
  output MemtoReg,
  output MemWrite,
  output ALUSrc,
  output RegWrite,
  output Jump
);

  wire ADDIU_out, Tipo_R_out;

  and J (Jump, ~OpCode[5], ~OpCode[4], ~OpCode[3], ~OpCode[2], OpCode[1], ~OpCode[0]);  // AND_Gate
  and BEQ (Branch, ~OpCode[5], ~OpCode[4], ~OpCode[3], OpCode[2], ~OpCode[1], ~OpCode[0]);  // AND_Gate
  and SW (MemWrite, OpCode[5], ~OpCode[4], OpCode[3], ~OpCode[2], OpCode[1], OpCode[0]);  // AND_Gate
  and LW (MemtoReg, OpCode[5], ~OpCode[4], ~OpCode[3], ~OpCode[2], OpCode[1], OpCode[0]);  // AND_Gate
  and ADDIU (ADDIU_out, ~OpCode[5], ~OpCode[4], OpCode[3], ~OpCode[2], ~OpCode[1], OpCode[0]);  // AND_Gate
  and Tipo_R (Tipo_R_out, ~OpCode[5], ~OpCode[4], ~OpCode[3], ~OpCode[2], ~OpCode[1], ~OpCode[0]);  // AND_Gate
  or or_1 (RegDst, ADDIU_out, MemtoReg);
  or or_2 (ALUSrc, ADDIU_out, MemtoReg, MemWrite);
  or or_3 (RegWrite, Tipo_R_out, ADDIU_out, MemtoReg);
endmodule

module UC_ula (
  input  [5:0] funct,
  input  [5:0] OpCode,
  output [2:0] ULAcode
);

  wire NOR0_out, nor_1_out, not_R_out, SLL0_out, SLT0_out, SUB0_out;

  and SLL0 (SLL0_out, ~funct[5], ~funct[4], ~funct[3], ~funct[2], ~funct[1], ~funct[0]);  // AND_Gate
  and SLT0 (SLT0_out, funct[5], ~funct[4], funct[3], ~funct[2], funct[1], ~funct[0]);  // AND_Gate
  and NOR0 (NOR0_out, funct[5], ~funct[4], ~funct[3], funct[2], funct[1], funct[0]);  // AND_Gate
  nand not_R (not_R_out, ~OpCode[0], ~OpCode[1], ~OpCode[2], ~OpCode[3], ~OpCode[4], ~OpCode[5]);  // NAND_Gate
  and SUB0 (SUB0_out, funct[5], ~funct[4], ~funct[3], ~funct[2], funct[1], ~funct[0]);  // AND_Gate
  or or_1 (ULAcode[0], NOR0_out, SLL0_out);
  or or_2 (ULAcode[1], SLT0_out, SLL0_out);
  nor nor_1 (nor_1_out, SUB0_out, NOR0_out, SLT0_out, SLL0_out);
  or or_3 (ULAcode[2], nor_1_out, not_R_out);
endmodule

module DataStorage (
  input  [2:0] Index,
  input  [31:0] WriteData0,
  input  [31:0] WriteData1,
  input  [31:0] WriteData2,
  input  [31:0] WriteData3,
  input  WriteEnable,
  input  Clock,
  output [31:0] ReadData0,
  output [31:0] ReadData1,
  output [31:0] ReadData2,
  output [31:0] ReadData3
);

  RAM #(.addrWidth(3), .dataWidth(32)) ram_1 (
    .addr(Index), .we(WriteEnable), .clk(Clock), .din(WriteData0), .dout(ReadData0));  // open: oe
  RAM #(.addrWidth(3), .dataWidth(32)) ram_2 (
    .addr(Index), .we(WriteEnable), .clk(Clock), .din(WriteData1), .dout(ReadData1));  // open: oe
  RAM #(.addrWidth(3), .dataWidth(32)) ram_3 (
    .addr(Index), .we(WriteEnable), .clk(Clock), .din(WriteData2), .dout(ReadData2));  // open: oe
  RAM #(.addrWidth(3), .dataWidth(32)) ram_4 (
    .addr(Index), .we(WriteEnable), .clk(Clock), .din(WriteData3), .dout(ReadData3));  // open: oe
endmodule

module CacheController (
  input  [1:0] word_counter,
  input  cpu_read,
  input  cpu_write,
  input  cache_hit,
  input  cache_dirty,
  input  mem_ready,
  input  clock,
  input  reset,
  output [2:0] state_debug,
  output cpu_ready,
  output mem_read,
  output mem_write,
  output update_cache,
  output set_dirty,
  output clear_dirty,
  output set_valid,
  output word_cnt_enable,
  output word_cnt_reset,
  output start_transfer,
  output transfer_done
);

  wire [1:0] WordCounter_q;
  wire [2:0] multiplexer_1_out, NextStateROM_data;

  ROM #(.addrWidth(9), .dataWidth(3)) NextStateROM (
    .addr({word_counter, cpu_write, cache_hit, cache_dirty, mem_ready, state_debug}), .data(NextStateROM_data));
  Multiplexer #(.width(3)) multiplexer_1 (.in0(3'b000), .in1(NextStateROM_data), .out(multiplexer_1_out), .sel(reset));
  Register #(.width(3)) StateReg (.D(multiplexer_1_out), .Q(state_debug), .clk(clock));  // open: en, clr
  ROM #(.addrWidth(3), .dataWidth(10)) ControlROM (
    .addr(state_debug),
    .data({start_transfer, word_cnt_reset, word_cnt_enable, set_valid, clear_dirty, set_dirty, update_cache, mem_write, mem_read, cpu_ready}));
  Counter #(.max('h3), .width(2)) WordCounter (
    .count(word_cnt_enable), .Q(WordCounter_q), .clk(clock), .clr(word_cnt_reset));  // open: load, D, carry, up
  Comparator #(.width(2)) comparator_1 (.a(WordCounter_q), .b(2'b11), .eq(transfer_done));  // open: gt, lt
endmodule

module AddressDecoder (
  input  [19:0] address,
  output [14:0] tag,
  output [2:0] index,
  output [1:0] offset
);


  assign index = address[4:2];
  assign offset = address[1:0];
  assign tag = address[19:5];
endmodule

module TagComparator (
  input  [14:0] tag_address,
  input  [14:0] tag_stored,
  input  valid_bit,
  output hit
);

  wire comparator_1_eq;

  Comparator #(.width(15)) comparator_1 (.a(tag_address), .b(tag_stored), .eq(comparator_1_eq));  // open: gt, lt
  and and_1 (hit, comparator_1_eq, valid_bit);
endmodule

module CacheLineStorage (
  input  write_enable,
  input  [2:0] index,
  input  clock,
  input  dirty_in,
  input  [14:0] tag_in,
  input  valid_in,
  input  [31:0] word0_in,
  input  [31:0] word1_in,
  input  [31:0] word2_in,
  input  [31:0] word3_in,
  output valid_out,
  output dirty_out,
  output [14:0] tag_out,
  output [31:0] word0_out,
  output [31:0] word1_out,
  output [31:0] word2_out,
  output [31:0] word3_out
);

  RAM #(.addrWidth(3), .dataWidth(17)) MetaRAM (
    .addr(index), .we(write_enable), .clk(clock), .din({dirty_in, tag_in, valid_in}),
    .dout({dirty_out, tag_out, valid_out}));  // open: oe
  RAM #(.addrWidth(3), .dataWidth(32)) Word0_RAM (
    .addr(index), .we(write_enable), .clk(clock), .din(word0_in), .dout(word0_out));  // open: oe
  RAM #(.addrWidth(3), .dataWidth(32)) Word1_RAM (
    .addr(index), .we(write_enable), .clk(clock), .din(word1_in), .dout(word1_out));  // open: oe
  RAM #(.addrWidth(3), .dataWidth(32)) Word2_RAM (
    .addr(index), .we(write_enable), .clk(clock), .din(word2_in), .dout(word2_out));  // open: oe
  RAM #(.addrWidth(3), .dataWidth(32)) Word3_RAM (
    .addr(index), .we(write_enable), .clk(clock), .din(word3_in), .dout(word3_out));  // open: oe
endmodule

module WordSelector (
  input  [31:0] word0,
  input  [31:0] word1,
  input  [31:0] word2,
  input  [31:0] word3,
  input  [1:0] offset,
  output [31:0] word_out
);

  Multiplexer #(.select(2), .width(32)) multiplexer_1 (
    .in0(word0), .in1(word1), .in2(word2), .in3(word3), .out(word_out), .sel(offset));
endmodule

module BlockTransferController (
  input  start_transfer,
  input  clock,
  input  [19:0] base_address,
  input  [31:0] word0_in,
  input  [31:0] word1_in,
  input  [31:0] word2_in,
  input  [31:0] word3_in,
  input  transfer_type,
  output transfer_done,
  output [19:0] mem_address,
  output [31:0] mem_data_out,
  output mem_read,
  output mem_write
);

  wire comparator_1_gt;
  wire [1:0] WordCounter_q;
  wire [19:0] bit_extender_1_out;

  Counter #(.max('h3), .width(2)) WordCounter (
    .count(start_transfer), .Q(WordCounter_q), .clk(clock));  // open: load, D, carry, up, clr
  assign bit_extender_1_out = {{18{WordCounter_q[1]}}, WordCounter_q};  // Bit_Extender bit_extender_1
  Comparator #(.width(2)) comparator_1 (.a(WordCounter_q), .b(2'b11), .gt(comparator_1_gt));  // open: eq, lt
  Multiplexer #(.select(2), .width(32)) multiplexer_1 (
    .in0(word0_in), .in1(word1_in), .in2(word2_in), .in3(word3_in), .out(mem_data_out), .sel(WordCounter_q));
  and and_1 (transfer_done, comparator_1_gt, ~start_transfer);  // AND_Gate
  Adder #(.width(20)) adder_1 (.a(bit_extender_1_out), .b(base_address), .out(mem_address));  // open: cin, cout
  and and_2 (mem_read, ~transfer_type, start_transfer);  // AND_Gate
  and and_3 (mem_write, transfer_type, start_transfer);
endmodule

module BlockAssembler (
  input  [31:0] word_in,
  input  [1:0] word_index,
  input  write_enable,
  input  clock,
  output [31:0] word0_out,
  output [31:0] word1_out,
  output [31:0] word2_out,
  output [31:0] word3_out
);

  wire demultiplexer_1_out0, demultiplexer_1_out1, demultiplexer_1_out2, demultiplexer_1_out3;

  Demultiplexer #(.select(2)) demultiplexer_1 (
    .out0(demultiplexer_1_out0), .out1(demultiplexer_1_out1), .out2(demultiplexer_1_out2),
    .out3(demultiplexer_1_out3), .in(write_enable), .sel(word_index));
  Register #(.width(32)) Word0_Reg (.D(word_in), .en(demultiplexer_1_out0), .Q(word0_out), .clk(clock));  // open: clr
  Register #(.width(32)) Word1_Reg (.D(word_in), .en(demultiplexer_1_out1), .Q(word1_out), .clk(clock));  // open: clr
  Register #(.width(32)) Word2_Reg (.D(word_in), .en(demultiplexer_1_out2), .Q(word2_out), .clk(clock));  // open: clr
  Register #(.width(32)) Word3_Reg (.D(word_in), .en(demultiplexer_1_out3), .Q(word3_out), .clk(clock));  // open: clr
endmodule

module CacheMemory (
  input  [19:0] cpu_address,
  input  cpu_mem_read,
  input  cpu_mem_write,
  input  mem_ready,
  input  clock,
  input  reset,
  input  [31:0] mem_read_data,
  output [2:0] state_debug,
  output cpu_ready,
  output [19:0] mem_address,
  output [31:0] mem_write_data,
  output mem_read,
  output mem_write,
  output [31:0] cpu_read_data
);

  wire and_1_out, cachecontroller_1_set_dirty, cachecontroller_1_set_valid, cachecontroller_1_start_transfer,
       cachecontroller_1_transfer_done, cachecontroller_1_update_cache, cachecontroller_1_word_cnt_enable,
       cachecontroller_1_word_cnt_reset, cachelinestorage_1_dirty_out, cachelinestorage_1_valid_out,
       or_1_out, tagcomparator_1_hit;
  wire [1:0] addressdecoder_1_offset, undriven;
  wire [14:0] cachelinestorage_1_tag_out;
  wire [19:2] addressdecoder_1_index;
  wire [31:0] blockassembler_1_word0_out, blockassembler_1_word1_out, blockassembler_1_word2_out,
       blockassembler_1_word3_out, cachelinestorage_1_word0_out, cachelinestorage_1_word1_out,
       cachelinestorage_1_word2_out, cachelinestorage_1_word3_out, wordselector_1_word_out;

  and and_1 (and_1_out, cpu_mem_write, tagcomparator_1_hit);
  AddressDecoder addressdecoder_1 (
    .address(cpu_address), .tag(addressdecoder_1_index[19:5]), .index(addressdecoder_1_index[4:2]),
    .offset(addressdecoder_1_offset));
  CacheController cachecontroller_1 (
    .word_counter(undriven), .cpu_read(cpu_mem_read), .cpu_write(cpu_mem_write),
    .cache_hit(tagcomparator_1_hit), .cache_dirty(cachelinestorage_1_dirty_out), .mem_ready(mem_ready),
    .clock(clock), .reset(reset), .state_debug(state_debug), .cpu_ready(cpu_ready),
    .update_cache(cachecontroller_1_update_cache), .set_dirty(cachecontroller_1_set_dirty),
    .set_valid(cachecontroller_1_set_valid), .word_cnt_enable(cachecontroller_1_word_cnt_enable),
    .word_cnt_reset(cachecontroller_1_word_cnt_reset), .start_transfer(cachecontroller_1_start_transfer),
    .transfer_done(cachecontroller_1_transfer_done));  // open: mem_read, mem_write, clear_dirty
  BlockAssembler blockassembler_1 (
    .word_in(mem_read_data), .word_index(undriven), .write_enable(cachecontroller_1_word_cnt_enable),
    .clock(clock), .word0_out(blockassembler_1_word0_out), .word1_out(blockassembler_1_word1_out),
    .word2_out(blockassembler_1_word2_out), .word3_out(blockassembler_1_word3_out));
  or or_1 (or_1_out, cachecontroller_1_update_cache, and_1_out);
  CacheLineStorage cachelinestorage_1 (
    .write_enable(or_1_out), .index(addressdecoder_1_index[4:2]), .clock(clock),
    .dirty_in(cachecontroller_1_set_dirty), .tag_in(addressdecoder_1_index[19:5]),
    .valid_in(cachecontroller_1_set_valid), .word0_in(blockassembler_1_word0_out),
    .word1_in(blockassembler_1_word1_out), .word2_in(blockassembler_1_word2_out),
    .word3_in(blockassembler_1_word3_out), .valid_out(cachelinestorage_1_valid_out),
    .dirty_out(cachelinestorage_1_dirty_out), .tag_out(cachelinestorage_1_tag_out),
    .word0_out(cachelinestorage_1_word0_out), .word1_out(cachelinestorage_1_word1_out),
    .word2_out(cachelinestorage_1_word2_out), .word3_out(cachelinestorage_1_word3_out));
  TagComparator tagcomparator_1 (
    .tag_address(addressdecoder_1_index[19:5]), .tag_stored(cachelinestorage_1_tag_out),
    .valid_bit(cachelinestorage_1_valid_out), .hit(tagcomparator_1_hit));
  LED Cache_Hit (.in(tagcomparator_1_hit));
  WordSelector wordselector_1 (
    .word0(cachelinestorage_1_word0_out), .word1(cachelinestorage_1_word1_out),
    .word2(cachelinestorage_1_word2_out), .word3(cachelinestorage_1_word3_out),
    .offset(addressdecoder_1_offset), .word_out(wordselector_1_word_out));
  Multiplexer #(.width(32)) multiplexer_1 (
    .in0(wordselector_1_word_out), .in1(mem_read_data), .out(cpu_read_data), .sel(tagcomparator_1_hit));
  BlockTransferController blocktransfercontroller_1 (
    .start_transfer(cachecontroller_1_start_transfer), .clock(clock),
    .base_address({addressdecoder_1_index, 2'b00}), .word0_in(cachelinestorage_1_word0_out),
    .word1_in(cachelinestorage_1_word1_out), .word2_in(cachelinestorage_1_word2_out),
    .word3_in(cachelinestorage_1_word3_out), .transfer_type(cachecontroller_1_transfer_done),
    .transfer_done(cachecontroller_1_transfer_done), .mem_address(mem_address),
    .mem_data_out(mem_write_data), .mem_read(mem_read), .mem_write(mem_write));
  LED Cache_Dirty ();  // open: in
endmodule
